# Fritzing sketch LiFi_Text_Transmitter (saved by Fritzing 0.9.3b)
circuit board: 8.46667cm x 5.64444cm
breadboards: 1

parts:
  Arduino = Arduino Uno (Rev3)
  LCM1602_IIC1 = LCM1602 IIC [part_number="LCM1602 IIC" chip_label="LCM1602 IIC" package="DIP (Dual Inline) [THT]"]
  LCD1 = LCD screen
  Keypad4x2 = Keypad Membran 4x4
  LD1 = LD

nets:
  N1: Arduino.A4/SDA, LCM1602_IIC1.SDA
  N2: Arduino.A5/SCL, LCM1602_IIC1.SCL
  N3: Arduino.D9_PWM, Keypad4x2.Pin4
  N4: Arduino.D10_PWM/SS, Keypad4x2.Pin3
  N5: Arduino.D11_PWM/MOSI, Keypad4x2.Pin2
  N6: Arduino.D12/MISO, Keypad4x2.Pin1
  N7: Arduino.D2, LD1.anode
  N8: Arduino.D3_PWM, Keypad4x2.Pin8
  N9: Arduino.D4, Keypad4x2.Pin7
  N10: Arduino.D5_PWM, Keypad4x2.Pin6
  N11: Arduino.D6_PWM, Keypad4x2.Pin5
  5V: Arduino.5V, LCM1602_IIC1.VCC
  GND: Arduino.GND, LCM1602_IIC1.GND, LD1.cathode
  VSS: LCM1602_IIC1.VSS, LCD1.VSS
  VDD: LCM1602_IIC1.VDD, LCD1.VDD
  N12: LCM1602_IIC1.V0, LCD1.V0
  N13: LCM1602_IIC1.RS, LCD1.RS
  N14: LCM1602_IIC1.RW, LCD1.R/W
  N15: LCM1602_IIC1.E, LCD1.E
  N16: LCM1602_IIC1.D0, LCD1.DB0
  N17: LCM1602_IIC1.D1, LCD1.DB1
  N18: LCM1602_IIC1.D2, LCD1.DB2
  N19: LCM1602_IIC1.D3, LCD1.DB3
  N20: LCM1602_IIC1.D4, LCD1.DB4
  N21: LCM1602_IIC1.D5, LCD1.DB5
  N22: LCM1602_IIC1.D6, LCD1.DB6
  N23: LCM1602_IIC1.D7, LCD1.DB7
  N24: LCM1602_IIC1.A, LCD1.LED+
  N25: LCM1602_IIC1.K, LCD1.LED-
  N26: LCM1602_IIC1.LED_A, LCM1602_IIC1.LED_B

custom parts:
  LCM1602 IIC: I2C-Module to use a 1602 or 2004 LCD on with the wire.h libory Serial LCD Modul
  Keypad Membran 4x4: Membrane Keypad 4x4 Matrix
  LD: A Generic Red Dot Laser Diode Module (~5mW)

// code stored in the sketch: AnalogReadSerial2LCD_LED.ino
#include <Wire.h>
#include <LiquidCrystal_I2C.h>

LiquidCrystal_I2C lcd(0x27, 16, 2);   // adress and format LCD

const int analogInPin = A0;           // Analog input pin that the potentiometer is attached to
const int analogOutPin = 9;           // Analog output pin that the LED is attached to

int sensorValue = 0;                  // value read from the pot
int outputValue = 0;                  // value output to the PWM (analog out)

void setup() {
  lcd.init();                         // init LCD
  lcd.backlight();
  lcd.home();
  lcd.setCursor(5, 0);                // place static text
  lcd.print("ADC = ");
  lcd.setCursor(15, 0);
  lcd.print("V");
  lcd.setCursor(0, 1);
  lcd.print("LED : ");
  lcd.setCursor(12, 1);
  lcd.print("%");
  Serial.begin(9600);                 // optional serial monitor
}

void loop() {
  int sensorValue = analogRead(analogInPin);          // read analog A0 en store in sensorValue
  float voltValue = 5.0 / 1024.0 * sensorValue;       // calculate volt at analog A0 and store in voltValue
  float percentValue = sensorValue / 1024.0 * 100.0;  // calculate percentage analog A0 and store in percentValue
  outputValue = map(sensorValue, 0, 1023, 0, 255);    // map analog input to analog output and store in outputValue
  analogWrite(analogOutPin, outputValue);             // write outputValue to analogOutPin

  lcd.setCursor(0, 0);                                // set cursor at deserid position
  leadingZeros(sensorValue, 4);                       // print sensorvalue with number of leading-characters (0 or space as specified in function leadingZeros)
  lcd.setCursor(10, 0);                               // set cursor at deserid position
  lcd.print(voltValue);                               // print voltValue
  lcd.setCursor(6, 1);                                // set cursor at deserid position
  lcd.print(percentValue);                            // print percentValue

  Serial.print("sensor = " );                         // print the results to the serial monitor:
  Serial.print(sensorValue);
  Serial.print("\t output = ");
  Serial.print(outputValue);
  Serial.print("\t procent = ");
  Serial.println(percentValue);

  delay(1000);                                        // set delay
}

void leadingZeros( int value, int width) {            // display result with leading characters
  char valueStr[6];                                   // large enough to hold an int
  itoa (value, valueStr, 10);                         // itoa converts int to string
  int len = strlen(valueStr);                         // calculate length of valueStr
  if (len < width) {
    len = width - len;
    while (len--)
      lcd.print(' ');                                 // for leading zeros place '0' between (), for leading spaces place ' ' between ()
  }
  lcd.print(valueStr);
}
